// Logisim project practica4.circ as structural Verilog: 6 circuits, main circuit Sumador 1 bit
module Sumador_y_restador_8_bits (
  input  C_in,
  input  [7:0] in_2,
  input  in_3,
  input  [7:0] in_4,
  output [7:0] out_5,
  output out_6
);

  wire restador_8_bits_1_c_out, sumador_8_bits_1_c_out;
  wire [7:0] restador_8_bits_1_out_4, sumador_8_bits_1_out_4;

  Sumador_8_bits sumador_8_bits_1 (
    .C_in(C_in), .in_2(in_2), .in_3(in_4), .out_4(sumador_8_bits_1_out_4), .C_out(sumador_8_bits_1_c_out));
  Restador_8_bits restador_8_bits_1 (
    .C_in(C_in), .A(in_2), .in_3(in_4), .out_4(restador_8_bits_1_out_4), .C_out(restador_8_bits_1_c_out));
  Multiplexer #(.width(8), .enable("false")) multiplexer_1 (
    .in0(sumador_8_bits_1_out_4), .in1(restador_8_bits_1_out_4), .out(out_5), .sel(in_3));
  Multiplexer #(.enable("false")) multiplexer_2 (
    .in0(sumador_8_bits_1_c_out), .in1(restador_8_bits_1_c_out), .out(out_6), .sel(in_3));

  // Notes on the sheet:
  //   A
  //   B
endmodule

module Sumador_1_bit (
  input  C_in,
  input  A,
  input  B,
  output A_B,
  output carry_C_out
);

  wire and_1_out, and_2_out, xor_1_out;

  xor xor_1 (xor_1_out, A, B);
  and and_1 (and_1_out, A, B);
  xor xor_2 (A_B, C_in, xor_1_out);
  and and_2 (and_2_out, C_in, xor_1_out);
  or or_1 (carry_C_out, and_2_out, and_1_out);
endmodule

module Sumador_8_bits (
  input  C_in,
  input  [7:0] in_2,
  input  [7:0] in_3,
  output [7:0] out_4,
  output C_out
);

  wire sumador_1_bit_1_carry_c_out, sumador_1_bit_2_carry_c_out, sumador_1_bit_3_carry_c_out,
       sumador_1_bit_4_carry_c_out, sumador_1_bit_5_carry_c_out, sumador_1_bit_6_carry_c_out,
       sumador_1_bit_7_carry_c_out;

  Sumador_1_bit sumador_1_bit_1 (
    .C_in(C_in), .A(in_2[0]), .B(in_3[0]), .A_B(out_4[0]), .carry_C_out(sumador_1_bit_1_carry_c_out));
  Sumador_1_bit sumador_1_bit_2 (
    .C_in(sumador_1_bit_1_carry_c_out), .A(in_2[1]), .B(in_3[1]), .A_B(out_4[1]),
    .carry_C_out(sumador_1_bit_2_carry_c_out));
  Sumador_1_bit sumador_1_bit_3 (
    .C_in(sumador_1_bit_2_carry_c_out), .A(in_2[2]), .B(in_3[2]), .A_B(out_4[2]),
    .carry_C_out(sumador_1_bit_3_carry_c_out));
  Sumador_1_bit sumador_1_bit_4 (
    .C_in(sumador_1_bit_3_carry_c_out), .A(in_2[3]), .B(in_3[3]), .A_B(out_4[3]),
    .carry_C_out(sumador_1_bit_4_carry_c_out));
  Sumador_1_bit sumador_1_bit_5 (
    .C_in(sumador_1_bit_4_carry_c_out), .A(in_2[4]), .B(in_3[4]), .A_B(out_4[4]),
    .carry_C_out(sumador_1_bit_5_carry_c_out));
  Sumador_1_bit sumador_1_bit_6 (
    .C_in(sumador_1_bit_5_carry_c_out), .A(in_2[5]), .B(in_3[5]), .A_B(out_4[5]),
    .carry_C_out(sumador_1_bit_6_carry_c_out));
  Sumador_1_bit sumador_1_bit_7 (
    .C_in(sumador_1_bit_6_carry_c_out), .A(in_2[6]), .B(in_3[6]), .A_B(out_4[6]),
    .carry_C_out(sumador_1_bit_7_carry_c_out));
  Sumador_1_bit sumador_1_bit_8 (
    .C_in(sumador_1_bit_7_carry_c_out), .A(in_2[7]), .B(in_3[7]), .A_B(out_4[7]), .carry_C_out(C_out));
endmodule

module Restador_1_bit (
  input  C_in,
  input  A,
  input  B,
  output A_B,
  output C_out
);

  wire and_1_out, and_2_out, not_1_out, xor_1_out, xor_2_out;

  not not_1 (not_1_out, B);
  xor xor_1 (xor_1_out, A, not_1_out);
  and and_1 (and_1_out, A, not_1_out);
  xor xor_2 (xor_2_out, C_in, xor_1_out);
  and and_2 (and_2_out, C_in, xor_1_out);
  xor xor_3 (A_B, 1'b1, xor_2_out);
  or or_1 (C_out, and_2_out, and_1_out);
endmodule

module Prueba (
  input  [7:0] in_1,
  input  [7:0] in_2,
  output [7:0] out_3
);

  Adder adder_1 (.a(in_1), .b(in_2), .out(out_3));  // open: cin, cout
endmodule

module Restador_8_bits (
  input  C_in,
  input  [7:0] A,
  input  [7:0] in_3,
  output [7:0] out_4,
  output C_out
);

  wire restador_1_bit_1_c_out, restador_1_bit_2_c_out, restador_1_bit_3_c_out, restador_1_bit_5_c_out,
       restador_1_bit_6_c_out, restador_1_bit_7_c_out;

  Restador_1_bit restador_1_bit_1 (.C_in(C_in), .A(A[0]), .B(in_3[0]), .A_B(out_4[0]), .C_out(restador_1_bit_1_c_out));
  Restador_1_bit restador_1_bit_2 (
    .C_in(restador_1_bit_1_c_out), .A(A[1]), .B(in_3[1]), .A_B(out_4[1]), .C_out(restador_1_bit_2_c_out));
  Restador_1_bit restador_1_bit_3 (
    .C_in(restador_1_bit_2_c_out), .A(A[2]), .B(in_3[2]), .A_B(out_4[2]), .C_out(restador_1_bit_3_c_out));
  Restador_1_bit restador_1_bit_4 (
    .C_in(restador_1_bit_3_c_out), .A(A[3]), .B(in_3[3]), .A_B(out_4[3]), .C_out(out_4[3]));
  Restador_1_bit restador_1_bit_5 (
    .C_in(out_4[3]), .A(A[4]), .B(in_3[4]), .A_B(out_4[4]), .C_out(restador_1_bit_5_c_out));
  Restador_1_bit restador_1_bit_6 (
    .C_in(restador_1_bit_5_c_out), .A(A[5]), .B(in_3[5]), .A_B(out_4[5]), .C_out(restador_1_bit_6_c_out));
  Restador_1_bit restador_1_bit_7 (
    .C_in(restador_1_bit_6_c_out), .A(A[6]), .B(in_3[6]), .A_B(out_4[6]), .C_out(restador_1_bit_7_c_out));
  Restador_1_bit restador_1_bit_8 (.C_in(restador_1_bit_7_c_out), .A(A[7]), .B(in_3[7]), .A_B(out_4[7]), .C_out(C_out));

  // Notes on the sheet:
  //   B
endmodule
